# Fritzing sketch Smoke Receiver Breadboard (saved by Fritzing 0.9.3b)
breadboards: 1

parts:
  Part1 = Arduino Pro Mini (5V)
  Part2 = Bluetooth Mate Silver
  LED1 = LED - 5mm [color="Red (633nm)" package="5 mm [THT]"]
  LED2 = LED - 5mm [color="Red (633nm)" package="5 mm [THT]"]
  LED3 = LED - 5mm [color="Red (633nm)" package="5 mm [THT]"]
  R1 = Resistor [tolerance=±5% resistance=470 package=THT]
  R2 = Resistor [tolerance=±5% resistance=470 package=THT]
  R3 = Resistor [tolerance=±5% resistance=470 package=THT]

nets:
  GND: Part1.GND, Part2.GND, R1.Pin_1, R2.Pin_0, R3.Pin_1
  VCC: Part1.VCC, Part2.VCC
  N1: LED1.cathode, R2.Pin_1
  N2: LED2.cathode, R3.Pin_0
  N3: LED3.cathode, R1.Pin_0
