# Fritzing sketch Smoke Sensor Breadboard (saved by Fritzing 0.9.3b)
breadboards: 1

parts:
  Part1 = Arduino Pro Mini v13
  Part3 = Bluetooth Mate Silver
  Route_battery_to_RAW_for_3_3v_operation = LIPO-1000mAh [package=lipo-1000]  # not connected
  U3 = GAS_SENSOR [package=mq-3]

nets:
  GND: Part1.GND, Part3.GND, U3.GND
  VCC: Part1.VCC, Part3.VCC, U3.5V
  N1: Part1.A0, U3.Vout
  N2: Part1.D13/SCK, Part3.RTS_5V
  N3: Part1.D12/MISO, Part3.RX_5V

custom parts:
  GAS_SENSOR: MQ-2 gas sensor
